// Digital circuit ControlUnit.dig as structural Verilog
module ControlUnit (
  input  [5:0] Opcode,
  input  Reset,
  output aluSrc,
  output RegDst,
  output [2:0] aluOp,
  output memToReg,
  output memRead,
  output memWrite,
  output RegWrite,
  output branch,
  output jump,
  output branch2
);

  wire Beq_eq, bne1, comparator_1_eq, comparator_2_eq, LW_eq, SW_eq;
  wire [2:0] priorityencoder_1_num;
  wire [11:0] multiplexer_1_out;

  Comparator #(.Bits(6)) comparator_1 (.a(Opcode), .b({6{1'b0}}), .eq(comparator_1_eq));  // open: gt, lt
  Comparator #(.Bits(6)) SW (.a(Opcode), .b(6'b101011), .eq(SW_eq));  // open: gt, lt
  Comparator #(.Bits(6)) LW (.a(Opcode), .b(6'b100011), .eq(LW_eq));  // open: gt, lt
  Comparator #(.Bits(6)) Beq (.a(Opcode), .b(6'b000100), .eq(Beq_eq));  // open: gt, lt
  Comparator #(.Bits(6)) Bne (.a(Opcode), .b(6'b000101), .eq(bne1));  // open: gt, lt
  Comparator #(.Bits(6)) comparator_2 (.a(Opcode), .b(6'b000010), .eq(comparator_2_eq));  // open: gt, lt
  PriorityEncoder #(.Selector_Bits(3)) priorityencoder_1 (
    .in0(comparator_1_eq), .in1(SW_eq), .in2(LW_eq), .in3(Beq_eq), .in4(bne1), .in5(comparator_2_eq),
    .in6(1'b0), .in7(1'b0), .num(priorityencoder_1_num));  // open: any
  Multiplexer #(.Selector_Bits(3), .Bits(12)) multiplexer_1 (
    .sel(priorityencoder_1_num), .in_0(12'h178), .in_1(12'h91), .in_2(12'h196), .in_3(12'h218),
    .in_4(12'h818), .in_5(12'h400), .in_6({12{1'b0}}), .in_7({12{1'b0}}), .out(multiplexer_1_out));
  Multiplexer #(.Bits(12)) multiplexer_2 (
    .sel(Reset), .in_0(multiplexer_1_out), .in_1({12{1'b0}}),
    .out({branch2, jump, branch, RegWrite, aluSrc, RegDst, aluOp, memToReg, memRead, memWrite}));

  // Other names for the same wires on the sheet: rst = Reset

  // Notes on the sheet:
  //   Reset: RESET input
endmodule
