// Digital circuit MIPS32SOC.dig as structural Verilog
module MIPS32SOC (
  input  clk,
  input  rst,
  output invalid_opcode,
  output invalid_addr,
  output invalid_pc
);

  wire aluSrc, and_1_out, and_2_out, branch, branch2, ctrl, isZero, jorbr, jump, memRead, memToReg, memWrite,
       not_1_out, readorwrite, RegDst, RegWrite;
  wire [1:0] dirvirtual_1_physicaladdress;
  wire [2:0] aluFunc, aluOp;
  wire [4:0] multiplexer_4_out;
  wire [5:0] Func, Opcode;
  wire [7:0] dirvirtual_1_physicaladdress_2;
  wire [10:0] datamemory_1_physicaladdress;
  wire [25:6] InstMem_d;
  wire [31:0] alu_1_res, beqoffset, bitextender_1_out, Data_Mem_d, jumpoffset, multiplexer_1_out,
       multiplexer_2_out, multiplexer_5_out, multiplexer_6_out, offset, offsetgeneral, PC_q, pcplus4,
       Reg_File_da, Reg_File_db;

  Multiplexer #(.Bits(32)) multiplexer_1 (.sel(rst), .in_0(pcplus4), .in_1(32'h400000), .out(multiplexer_1_out));
  Multiplexer #(.Bits(32)) multiplexer_2 (
    .sel(jorbr), .in_0(multiplexer_1_out), .in_1(offsetgeneral), .out(multiplexer_2_out));
  not not_1 (not_1_out, isZero);
  Register #(.Bits(32)) PC (.D(multiplexer_2_out), .C(clk), .en(1'b1), .Q(PC_q));
  Add #(.Bits(32)) add_1 (.a(pcplus4), .b(offset), .c_i(1'b0), .s(beqoffset));  // open: c_o
  DirVirtual dirvirtual_1 (
    .virtualPC(PC_q), .invalidMemory(invalid_pc),
    .Physicaladdress({dirvirtual_1_physicaladdress_2, dirvirtual_1_physicaladdress}));
  and and_1 (and_1_out, branch, isZero);
  and and_2 (and_2_out, branch2, not_1_out);
  or or_1 (ctrl, and_1_out, and_2_out);
  Add #(.Bits(32)) add_2 (.a(PC_q), .b(32'h4), .c_i(1'b0), .s(pcplus4));  // open: c_o
  ROM #(.AddrBits(8), .Bits(32)) InstMem (
    .A(dirvirtual_1_physicaladdress_2), .sel(1'b1), .D({Opcode, InstMem_d, Func}));
  ControlUnit controlunit_1 (
    .Opcode(Opcode), .Reset(rst), .aluSrc(aluSrc), .RegDst(RegDst), .aluOp(aluOp), .memToReg(memToReg),
    .memRead(memRead), .memWrite(memWrite), .RegWrite(RegWrite), .branch(branch), .jump(jump),
    .branch2(branch2));  // open: lup
  jtarget jtarget_1 (.jumpadress({InstMem_d, Func}), .pc_plus_4(pcplus4), .out(jumpoffset));
  Multiplexer #(.Bits(32)) multiplexer_3 (.sel(jump), .in_0(beqoffset), .in_1(jumpoffset), .out(offsetgeneral));
  Multiplexer #(.Bits(5)) multiplexer_4 (
    .sel(RegDst), .in_0(InstMem_d[20:16]), .in_1(InstMem_d[15:11]), .out(multiplexer_4_out));
  BitExtender #(.inputBits(16), .outputBits(32)) bitextender_1 (.in({InstMem_d[15:6], Func}), .out(bitextender_1_out));
  or or_2 (jorbr, jump, ctrl);
  RegisterFile #(.AddrBits(5), .Bits(32)) Reg_File (
    .Din(multiplexer_6_out), .we(RegWrite), .Rw(multiplexer_4_out), .C(clk), .Ra(InstMem_d[25:21]),
    .Rb(InstMem_d[20:16]), .Da(Reg_File_da), .Db(Reg_File_db));
  ShiftLeft2 shiftleft2_1 (.i(bitextender_1_out), .o(offset));
  Multiplexer #(.Bits(32)) multiplexer_5 (
    .sel(aluSrc), .in_0(Reg_File_db), .in_1(bitextender_1_out), .out(multiplexer_5_out));
  ALU alu_1 (.a(Reg_File_da), .b(multiplexer_5_out), .op(aluFunc), .res(alu_1_res), .isZero(isZero));
  RAMDualPort #(.AddrBits(9), .Bits(32)) Data_Mem (
    .A(datamemory_1_physicaladdress[10:2]), .Din(Reg_File_db), .str(memWrite), .C(clk), .ld(memRead),
    .D(Data_Mem_d));
  ALUControl alucontrol_1 (.aluOp(aluOp), .Func(Func), .aluFunc(aluFunc));
  Multiplexer #(.Bits(32)) multiplexer_6 (.sel(memToReg), .in_0(alu_1_res), .in_1(Data_Mem_d), .out(multiplexer_6_out));
  DataMemory datamemory_1 (
    .virtualPC(alu_1_res), .en(readorwrite), .invalidMemory(invalid_addr),
    .Physicaladdress(datamemory_1_physicaladdress));
  or or_3 (readorwrite, memRead, memWrite);

  assign invalid_opcode = 1'b0;

  // Other names for the same wires on the sheet: inv = invalid_addr; invalidmem = invalid_pc

  // Notes on the sheet:
  //   contents of InstMem (hex, n*v repeats v):
  //   10a7fffb,8000001,ac080008,0,0,0,0,0,8000001
endmodule
